# Fritzing sketch pcbcircuitboard (saved by Fritzing 0.9.3b)
circuit board: 5.42511cm x 4.06516cm
breadboards: 1

parts:
  Raspberry_Pi_1 = Raspberry Pi 3 [part_number=RPI-3-V1.2]
  JP2 = Header 12 [package=1x12_machine-pin-header_lock.004]

nets:
  N1: Raspberry_Pi_1.3v3, JP2.5
  N2: Raspberry_Pi_1.GPIO2, JP2.1, JP2.4
  N3: Raspberry_Pi_1.GPIO3, JP2.3
  N4: Raspberry_Pi_1.GND, JP2.6
